# Fritzing sketch awt_fritzing (saved by Fritzing 0.9.2b)
breadboards: 1

parts:
  PWR = Toggle Switch [package=THT]
  U1 = attiny85 [package=dip]
  RHT1 = Humidity and Temperature Sensor RHT03
  U2 = RF-LINK_TX [package=rf-link_tx]
  R2 = Resistor [tolerance=±5% resistance=220 package=THT]
  LED1 = LED - 3mm [color="Red (633nm)" package="3 mm [THT]"]
  RST = Pushbutton [package=THT]
  BAT1 = Battery Holders [package=battery-aa-kit]
  BAT2 = Battery Holders [package=battery-aa-kit]
  BAT3 = Battery Holders [package=battery-aa-kit]
  R3 = Resistor [tolerance=±5% resistance=10k package=THT]
  ANT1 = Antenna

nets:
  N1: PWR.L1, BAT3.+
  VCC: PWR.COM, U1.Pin_8, RHT1.Vcc, U2.+5V, R3.Pin_1
  N2: U1.Pin_1, RST.leg0
  N3: U1.Pin_4, RHT1.GND_2, U2.GND, R2.Pin_1, RST.leg1, BAT1.-
  N4: U1.Pin_5, RHT1.Data-signal, R3.Pin_0
  N5: U1.Pin_6, U2.DATA
  N6: U1.Pin_7, LED1.anode
  N7: U2.ANT, ANT1.antenna_lead
  N8: R2.Pin_0, LED1.cathode
  N9: BAT1.+, BAT2.-
  N10: BAT2.+, BAT3.-

notes:
  ON/OFF
